// Logisim project circuito flip flop.circ as structural Verilog: 1 circuit, main circuit main
module main (
  input  Enable,
  input  Data0,
  input  Data1,
  input  Data2,
  input  Data3,
  input  Data4,
  input  Data5,
  input  Data6,
  input  Data7,
  input  Data8,
  input  Data9,
  input  Data10,
  input  Data11,
  input  Data12,
  input  Data13,
  input  Data14,
  input  Data15,
  output out_18,
  output out_19,
  output out_20,
  output out_21,
  output out_22,
  output out_23,
  output out_24,
  output out_25,
  output out_26,
  output out_27,
  output out_28,
  output out_29,
  output out_30,
  output out_31,
  output out_32,
  output out_33,
  output out_34,
  output out_35,
  output out_36,
  output out_37,
  output out_38,
  output out_39,
  output out_40,
  output out_41,
  output out_42,
  output out_43,
  output out_44,
  output out_45,
  output out_46,
  output out_47,
  output out_48,
  output out_49
);

  wire nand_1_out, nand_3_out, nand_4_out, nand_6_out, nand_8_out, nand_9_out, nand_10_out, nand_12_out,
       nand_14_out, nand_15_out, nand_18_out, nand_20_out, nand_21_out, nand_23_out, nand_24_out,
       nand_26_out, nand_28_out, nand_29_out, nand_31_out, nand_33_out, nand_34_out, nand_36_out,
       nand_38_out, nand_39_out, nand_41_out, nand_43_out, nand_44_out, nand_46_out, nand_48_out,
       nand_49_out, nand_50_out, nand_52_out, nand_54_out, nand_55_out, nand_58_out, nand_60_out,
       nand_61_out, nand_63_out, nand_64_out, nand_66_out, nand_68_out, nand_69_out, nand_71_out,
       nand_73_out, nand_74_out, nand_76_out, nand_78_out, nand_79_out;

  nand nand_1 (nand_1_out, Data0, Enable);
  nand nand_2 (out_18, nand_1_out, out_19);
  nand nand_3 (nand_3_out, Data0, Data0);
  nand nand_4 (nand_4_out, nand_3_out, Enable);
  nand nand_5 (out_19, out_18, nand_4_out);
  nand nand_6 (nand_6_out, Data1, Enable);
  nand nand_7 (out_20, nand_6_out, out_21);
  nand nand_8 (nand_8_out, Data1, Data1);
  nand nand_9 (nand_9_out, Data2, Enable);
  nand nand_10 (nand_10_out, nand_8_out, Enable);
  nand nand_11 (out_21, out_20, nand_10_out);
  nand nand_12 (nand_12_out, Data2, Data2);
  nand nand_13 (out_22, nand_9_out, out_23);
  nand nand_14 (nand_14_out, nand_12_out, Enable);
  nand nand_15 (nand_15_out, Data3, Enable);
  nand nand_16 (out_24, nand_15_out, out_25);
  nand nand_17 (out_23, out_22, nand_14_out);
  nand nand_18 (nand_18_out, Data3, Data3);
  nand nand_19 (out_25, out_24, nand_20_out);
  nand nand_20 (nand_20_out, nand_18_out, Enable);
  nand nand_21 (nand_21_out, Data4, Enable);
  nand nand_22 (out_26, nand_21_out, out_27);
  nand nand_23 (nand_23_out, Data4, Data4);
  nand nand_24 (nand_24_out, nand_23_out, Enable);
  nand nand_25 (out_27, out_26, nand_24_out);
  nand nand_26 (nand_26_out, Data5, Enable);
  nand nand_27 (out_28, nand_26_out, out_29);
  nand nand_28 (nand_28_out, Data5, Data5);
  nand nand_29 (nand_29_out, nand_28_out, Enable);
  nand nand_30 (out_29, out_28, nand_29_out);
  nand nand_31 (nand_31_out, Data6, Enable);
  nand nand_32 (out_30, nand_31_out, out_31);
  nand nand_33 (nand_33_out, Data6, Data6);
  nand nand_34 (nand_34_out, nand_33_out, Enable);
  nand nand_35 (out_31, out_30, nand_34_out);
  nand nand_36 (nand_36_out, Data7, Enable);
  nand nand_37 (out_32, nand_36_out, out_33);
  nand nand_38 (nand_38_out, Data7, Data7);
  nand nand_39 (nand_39_out, nand_38_out, Enable);
  nand nand_40 (out_33, out_32, nand_39_out);
  nand nand_41 (nand_41_out, Data8, Enable);
  nand nand_42 (out_34, nand_41_out, out_35);
  nand nand_43 (nand_43_out, Data8, Data8);
  nand nand_44 (nand_44_out, nand_43_out, Enable);
  nand nand_45 (out_35, out_34, nand_44_out);
  nand nand_46 (nand_46_out, Data9, Enable);
  nand nand_47 (out_36, nand_46_out, out_37);
  nand nand_48 (nand_48_out, Data9, Data9);
  nand nand_49 (nand_49_out, Data10, Enable);
  nand nand_50 (nand_50_out, nand_48_out, Enable);
  nand nand_51 (out_37, out_36, nand_50_out);
  nand nand_52 (nand_52_out, Data10, Data10);
  nand nand_53 (out_38, nand_49_out, out_39);
  nand nand_54 (nand_54_out, nand_52_out, Enable);
  nand nand_55 (nand_55_out, Data11, Enable);
  nand nand_56 (out_39, out_38, nand_54_out);
  nand nand_57 (out_40, nand_55_out, out_41);
  nand nand_58 (nand_58_out, Data11, Data11);
  nand nand_59 (out_41, out_40, nand_60_out);
  nand nand_60 (nand_60_out, nand_58_out, Enable);
  nand nand_61 (nand_61_out, Data12, Enable);
  nand nand_62 (out_42, nand_61_out, out_43);
  nand nand_63 (nand_63_out, Data12, Data12);
  nand nand_64 (nand_64_out, nand_63_out, Enable);
  nand nand_65 (out_43, out_42, nand_64_out);
  nand nand_66 (nand_66_out, Data13, Enable);
  nand nand_67 (out_44, nand_66_out, out_45);
  nand nand_68 (nand_68_out, Data13, Data13);
  nand nand_69 (nand_69_out, nand_68_out, Enable);
  nand nand_70 (out_45, out_44, nand_69_out);
  nand nand_71 (nand_71_out, Data14, Enable);
  nand nand_72 (out_46, nand_71_out, out_47);
  nand nand_73 (nand_73_out, Data14, Data14);
  nand nand_74 (nand_74_out, nand_73_out, Enable);
  nand nand_75 (out_47, out_46, nand_74_out);
  nand nand_76 (nand_76_out, Data15, Enable);
  nand nand_77 (out_48, nand_76_out, out_49);
  nand nand_78 (nand_78_out, Data15, Data15);
  nand nand_79 (nand_79_out, nand_78_out, Enable);
  nand nand_80 (out_49, out_48, nand_79_out);
endmodule
